# Fritzing sketch autolight (saved by Fritzing 0.9.2b)
breadboards: 1

parts:
  Part1 = Photon
  R1 = Resistor [tolerance=±5% resistance=220 package=THT]
  S1 = Pushbutton [package="[THT]"]
  R2 = Photocell (LDR) [package=THT]
  LED1 = LED - 5mm [color="Red (633nm)" package="5 mm [THT]"]
  R3 = Resistor [tolerance=±5% resistance=220 package=THT]
  R4 = Resistor [tolerance=±5% resistance=220 package=THT]
  J1 = Infrared Proximity Sensor
  7_Segment1 = 7 Segment Display  # not connected

nets:
  N1: Part1.A0, R2.pin_1, R3.Pin_1
  N2: Part1.A3, J1.Vout
  N3: Part1.A4, S1.Pin_1, S1.Pin_2, R4.Pin_0
  N4: Part1.A5, LED1.anode
  GND: Part1.GND, R2.pin_0, LED1.cathode, R4.Pin_1, J1.GND
  N5: Part1.D0, Part1.D1, Part1.D2, Part1.D3, Part1.D4, Part1.D5, Part1.D6, Part1.D7, R1.Pin_0
  N6: Part1.3V3, R1.Pin_1, S1.Pin_3, S1.Pin_4, R3.Pin_0
